// Logisim project cpu.circ as structural Verilog: 1 circuit, main circuit cpu
module cpu (
  input  clk,
  input  [31:0] Instruction,
  input  [31:0] MemReadData,
  output [31:0] MemAddress,
  output [31:0] ProgramCounter,
  output [31:0] ra,
  output [31:0] sp,
  output [31:0] t0,
  output [31:0] t1,
  output [31:0] t2,
  output [31:0] s0,
  output [31:0] s1,
  output [31:0] a0,
  output [3:0] MemWriteMask,
  output [31:0] MemWriteData
);

  wire ASel, BrEq, BrLt, BrUn, BSel, comparator_1_eq, comparator_2_eq, comparator_3_gt, comparator_4_eq,
       comparator_5_eq, comparator_6_eq, comparator_7_gt, comparator_8_eq, is_ALUForward, is_MemForward,
       PCSel_EX, PCSel_IF;
  wire [1:0] Forward_Control;
  wire [2:0] funct3;
  wire [3:0] ALUSel;
  wire [6:0] funct7;
  wire [14:0] Control, Control_EX, Control_MEM, Control_WB;
  wire [24:0] Instruction_ID;
  wire [31:0] ALUResult, ALUResult_EX, Immediate, Instruction_EX, Instruction_MEM, Instruction_WB, LoadData,
       multiplexer_1_out, multiplexer_3_out, multiplexer_4_out, NextPC, NextPC_EX, NextPC_ID, NextPC_MEM,
       PC_EX, PC_ID, ReadData1, ReadData1_EX, ReadData2, ReadData2_EX, ReadData2_MEM, SelectInstruction,
       WriteBack, WriteBack_ID;

  Adder #(.width(32)) adder_1 (.a(ProgramCounter), .b(32'h4), .out(NextPC));  // open: cin, cout
  Multiplexer #(.width(32)) multiplexer_1 (.in0(NextPC), .in1(ALUResult_EX), .out(multiplexer_1_out), .sel(PCSel_IF));
  Register #(.width(32)) PC (.D(multiplexer_1_out), .clk(clk), .Q(ProgramCounter));  // open: en, clr
  Multiplexer #(.width(32)) multiplexer_2 (.in0(Instruction), .in1(32'h13), .out(SelectInstruction), .sel(Control[0]));
  Register #(.width(32)) register_1 (.D(NextPC), .clk(clk), .Q(NextPC_ID));  // open: en, clr
  Register #(.width(32)) register_2 (.D(ProgramCounter), .clk(clk), .Q(PC_ID));  // open: en, clr
  Register #(.width(32)) register_3 (
    .D(SelectInstruction), .clk(clk), .Q({funct7, Instruction_ID[24:15], funct3, Instruction_ID[11:0]}));  // open: en, clr
  control_logic control_logic_1 (
    .Instruction({funct7, Instruction_ID[24:15], funct3, Instruction_ID[11:0]}), .BrEq(BrEq), .BrLt(BrLt),
    .PCSel(Control[0]), .RegWEn(Control[1]), .ImmSel(Control[4:2]), .BrUn(BrUn), .ASel(ASel), .BSel(BSel),
    .ALUSel(ALUSel), .MemRW(Control[12]), .WBSel(Control[14:13]));
  Comparator #(.mode("unsigned"), .width(2)) comparator_1 (
    .a(Control_WB[14:13]), .b(2'b00), .eq(comparator_1_eq));  // open: gt, lt
  Comparator #(.mode("unsigned"), .width(1)) comparator_2 (
    .a(Control_WB[1]), .b(1'b1), .eq(comparator_2_eq));  // open: gt, lt
  Comparator #(.mode("unsigned"), .width(5)) comparator_3 (
    .a(Instruction_WB[11:7]), .b({5{1'b0}}), .gt(comparator_3_gt));  // open: eq, lt
  Comparator #(.mode("unsigned"), .width(5)) comparator_4 (
    .a(Instruction_WB[11:7]), .b(Instruction_EX[19:15]), .eq(comparator_4_eq));  // open: gt, lt
  Comparator #(.mode("unsigned"), .width(2)) comparator_5 (
    .a(Control_MEM[14:13]), .b(2'b01), .eq(comparator_5_eq));  // open: gt, lt
  Comparator #(.mode("unsigned"), .width(1)) comparator_6 (
    .a(Control_MEM[1]), .b(1'b1), .eq(comparator_6_eq));  // open: gt, lt
  Comparator #(.mode("unsigned"), .width(5)) comparator_7 (
    .a(Instruction_MEM[11:7]), .b({5{1'b0}}), .gt(comparator_7_gt));  // open: eq, lt
  Comparator #(.mode("unsigned"), .width(5)) comparator_8 (
    .a(Instruction_MEM[11:7]), .b(Instruction_EX[19:15]), .eq(comparator_8_eq));  // open: gt, lt
  and and_1 (is_MemForward, comparator_1_eq, comparator_2_eq, comparator_3_gt, comparator_4_eq);
  and and_2 (is_ALUForward, comparator_5_eq, comparator_6_eq, comparator_7_gt, comparator_8_eq);
  regfile regfile_1 (
    .ReadIndex1(Instruction_ID[19:15]), .ReadIndex2(Instruction_ID[24:20]),
    .WriteIndex(Instruction_ID[11:7]), .WriteData(WriteBack_ID), .RegWEn(Control[1]), .clk(clk), .ra(ra),
    .sp(sp), .t0(t0), .t1(t1), .t2(t2), .s0(s0), .s1(s1), .a0(a0), .ReadData1(ReadData1),
    .ReadData2(ReadData2));
  Priority_Encoder #(.select_enc(2)) priority_encoder_1 (
    .in0(Control_EX[6]), .in1(Control_EX[6]), .in2(is_MemForward), .in3(is_ALUForward), .out(Forward_Control));  // open: gs, en_out, en_in
  Register #(.width(32)) register_4 (.D(NextPC_ID), .clk(clk), .Q(NextPC_EX));  // open: en, clr
  Register #(.width(32)) register_5 (.D(PC_ID), .clk(clk), .Q(PC_EX));  // open: en, clr
  Register #(.width(32)) register_6 (.D(ReadData1), .clk(clk), .Q(ReadData1_EX));  // open: en, clr
  Register #(.width(32)) register_7 (.D(ReadData2), .clk(clk), .Q(ReadData2_EX));  // open: en, clr
  Register #(.width(32)) register_8 (
    .D({funct7, Instruction_ID[24:15], funct3, Instruction_ID[11:0]}), .clk(clk), .Q(Instruction_EX));  // open: en, clr
  Register #(.width(15)) register_9 (
    .D({Control[14:12], ALUSel, BSel, ASel, BrUn, Control[4:0]}), .clk(clk), .Q(Control_EX));  // open: en, clr
  Register #(.width(1)) register_10 (.D(Control[0]), .clk(clk), .Q(PCSel_EX));  // open: en, clr
  Multiplexer #(.select(2), .width(32)) multiplexer_3 (
    .in0(ReadData1_EX), .in1(PC_EX), .in2(MemAddress), .in3(WriteBack_ID), .out(multiplexer_3_out),
    .sel(Forward_Control));
  Multiplexer #(.width(32)) multiplexer_4 (
    .in0(ReadData2_EX), .in1(Immediate), .out(multiplexer_4_out), .sel(Control_EX[7]));
  imm_gen imm_gen_1 (.Instruction(Instruction_EX), .ImmSel(Control_EX[4:2]), .Immediate(Immediate));
  branch_comp branch_comp_1 (
    .BrData1(ReadData1_EX), .BrData2(ReadData2_EX), .BrUn(Control_EX[5]), .BrEq(BrEq), .BrLt(BrLt));
  alu alu_1 (.A(multiplexer_3_out), .B(multiplexer_4_out), .ALUSel(Control_EX[11:8]), .ALUResult(ALUResult));
  Register #(.width(32)) register_11 (.D(NextPC_EX), .clk(clk), .Q(NextPC_MEM));  // open: en, clr
  Register #(.width(32)) register_12 (.D(ALUResult), .clk(clk), .Q(MemAddress));  // open: en, clr
  Register #(.width(32)) register_13 (.D(ReadData2_EX), .clk(clk), .Q(ReadData2_MEM));  // open: en, clr
  Register #(.width(32)) register_14 (.D(Instruction_EX), .clk(clk), .Q(Instruction_MEM));  // open: en, clr
  Register #(.width(15)) register_15 (.D(Control_EX), .clk(clk), .Q(Control_MEM));  // open: en, clr
  Register #(.width(1)) register_16 (.D(PCSel_EX), .clk(clk), .Q(PCSel_IF));  // open: en, clr
  partial_store partial_store_1 (
    .Instruction(Instruction_MEM), .MemAddress(MemAddress), .DataFromReg(ReadData2_MEM),
    .MemRW(Control_MEM[12]), .MemWriteMask(MemWriteMask), .DataToMem(MemWriteData));
  partial_load partial_load_1 (
    .Instruction(Instruction_MEM), .MemAddress(MemAddress), .DataFromMem(MemReadData), .DataToReg(LoadData));
  Multiplexer #(.select(2), .width(32)) multiplexer_5 (
    .in0(LoadData), .in1(MemAddress), .in2(NextPC_MEM), .out(WriteBack), .sel(Control_MEM[14:13]));  // open: in3
  Register #(.width(32)) register_17 (.D(WriteBack), .clk(clk), .Q(WriteBack_ID));  // open: en, clr
  Register #(.width(32)) register_18 (.D(Instruction_MEM), .clk(clk), .Q(Instruction_WB));  // open: en, clr
  Register #(.width(15)) register_19 (.D(Control_MEM), .clk(clk), .Q(Control_WB));  // open: en, clr

  // Other names for the same wires on the sheet: ALUResult_MEM[31:0] = MemAddress; PCSel = Control[0];
  //   RegWEn = Control[1]; ImmSel[2:0] = Control[4:2]; Control[11:5] = {ALUSel, BSel, ASel, BrUn};
  //   MemRW = Control[12]; WBSel[1:0] = Control[14:13]; is_PC = Control_EX[6]; is_ReadData1 = Control_EX[6];
  //   opcode[6:0] = Instruction_ID[6:0]; rd[4:0] = Instruction_ID[11:7];
  //   Instruction_ID (some bits) = {funct7, funct3}; rs1[4:0] = Instruction_ID[19:15];
  //   rs2[4:0] = Instruction_ID[24:20]

  // Notes on the sheet:
  //   To IMEM
  //   IMEM (do **NOT** move this)
  //   From IMEM
  //   Control Logic Pipelining
  //   Additional Control Logic for Forwarding
  //   Inputs/Outputs for testing. Do **NOT** move these.
  //   It is OK to move the PC, RegFile, ALU, MEM, Branch Comp, Imm Gen, Partial Load, Partial Store and Control Logic to wherever is most convenient for you when constructing your CPU, and to delete this text
  //   To DMEM
  //   DMEM (do **NOT** move this)
  //   From DMEM
endmodule
